# Fritzing sketch tankniveau (saved by Fritzing 1.0.1rc)
breadboards: 1

parts:
  Heltec_WiFi_LoRa_1 = Heltec WiFi LoRa 32 [part_number=HTIT-WB32LA]
  DS1 = DS18B20 1-Wire Temperature Sensor [part_number=DS18B20]
  DS2 = DS18B20 1-Wire Temperature Sensor [part_number=DS18B20]
  DS3 = DS18B20 1-Wire Temperature Sensor [part_number=DS18B20]
  DS4 = DS18B20 1-Wire Temperature Sensor [part_number=DS18B20]
  R1 = Resistor [tolerance=±5% power=0.25W resistance=4.7k package=THT]
  USSM1 = Ultrasonic Sensor Module with cable

nets:
  N1: Heltec_WiFi_LoRa_1.pin_3, USSM1.IO
  VDD: Heltec_WiFi_LoRa_1.pin_16, Heltec_WiFi_LoRa_1.pin_21, DS1.VDD, DS2.VDD, DS3.VDD, DS4.VDD, R1.Pin_0
  N2: Heltec_WiFi_LoRa_1.pin_17, Heltec_WiFi_LoRa_1.pin_20
  GND: Heltec_WiFi_LoRa_1.pin_18, Heltec_WiFi_LoRa_1.pin_19, Heltec_WiFi_LoRa_1.pin_22, DS1.GND, DS2.GND, DS3.GND, DS4.GND, USSM1.GND
  N3: Heltec_WiFi_LoRa_1.pin_27, DS1.DQ, DS2.DQ, DS3.DQ, DS4.DQ, R1.Pin_1
  N4: Heltec_WiFi_LoRa_1.pin_35, USSM1.Vsup

custom parts:
  Heltec WiFi LoRa 32: Heltec WiFi LoRa 32 WiFi LoRa 32 is a classic IoT dev-board designed & produced by Heltec Automation(TM). It’s a highly integrated product based on ESP32 + SX127x, it has Wi-Fi, BLE, LoRa functions, also Li-Po battery management system, 0.96″ OLED are also included. It’s the best choice for smart cities, smart farms, smart home, and IoT makers.
